# Fritzing sketch user-panel (saved by Fritzing 0.9.3b)
circuit board: 8.46667cm x 5.64444cm

parts:
  Part2 = Arduino Nano (Rev3.0)
  Part3 = Bluetooth HM-10
  LCD1 = LCD screen SD1602VBWB-XA-G-G
  S1 = Pushbutton [package="[SMD]"]
  S2 = Pushbutton [package="[SMD]"]
  S3 = Pushbutton [package="[SMD]"]
  S4 = Pushbutton [package="[SMD]"]
  R1 = Resistor [tolerance=±5% resistance=220 package="2010 [SMD]"]
  J1 = female pin header, 2 pins [form="♀ (female)"]
  J2 = female pin header, 2 pins [form="♀ (female)"]

nets:
  N1: Part2.D1/TX, Part3.RXD
  N2: Part2.D0/RX, Part3.TXD, Part3.BRK
  GND: Part2.GND, Part3.GND, LCD1.VSS, LCD1.R/W, LCD1.LED-, J1.pin2
  N3: Part2.D7, LCD1.E
  N4: Part2.D8, LCD1.RS
  N5: Part2.D9, LCD1.DB4
  N6: Part2.D10, LCD1.DB5
  N7: Part2.D11/MOSI, LCD1.DB6
  N8: Part2.D12/MISO, LCD1.DB7
  N9: Part2.VIN, J1.pin1
  N10: Part2.5V, R1.Pin_0
  N11: Part2.A5, J2.pin1
  N12: Part2.A4, J2.pin2
  3V3: Part2.A3, Part2.A2, Part2.A1, Part2.A0, Part2.3V3, Part3.VCC, S1.Pin_3, S1.Pin_4, S2.Pin_3, S2.Pin_4, S3.Pin_3, S3.Pin_4, S4.Pin_3, S4.Pin_4
  N13: LCD1.LED+, R1.Pin_1

notes:
  Same power supply for all MCU
  I2C wires to connect all MCU

custom parts:
  LCD screen SD1602VBWB-XA-G-G: A standard character display, usually with 2x16 characters based on Lionel Michel's LCD display.
